// Logisim project Lab2.circ as structural Verilog
module Xor (
  input  X,
  input  Y,
  output out_3
);

  wire and_1_out, and_2_out, not_1_out, not_2_out;

  not not_1 (not_1_out, X);
  and and_1 (and_1_out, not_1_out, Y);
  and and_2 (and_2_out, X, not_2_out);
  not not_2 (not_2_out, Y);
  or or_1 (out_3, and_1_out, and_2_out);
endmodule

module HalfAdder (
  input  A,
  input  B,
  output S,
  output C
);

  Xor xor_1 (.X(A), .Y(B), .out_3(S));
  and and_1 (C, A, B);
endmodule

module FullAdder (
  input  A,
  input  B,
  input  C,
  output S,
  output C_2
);

  wire halfadder_1_c, halfadder_2_c, halfadder_2_s;

  HalfAdder halfadder_1 (.A(A), .B(halfadder_2_s), .S(S), .C(halfadder_1_c));
  HalfAdder halfadder_2 (.A(B), .B(C), .S(halfadder_2_s), .C(halfadder_2_c));
  or or_1 (C_2, halfadder_1_c, halfadder_2_c);
endmodule

module _2_MUX (
  input  A,
  input  B,
  input  Sel,
  output Y
);

  wire and_1_out, and_2_out, not_1_out;

  not not_1 (not_1_out, Sel);
  and and_1 (and_1_out, A, not_1_out);
  and and_2 (and_2_out, B, Sel);
  or or_1 (Y, and_1_out, and_2_out);
endmodule

module _4_MUX (
  input  A,
  input  B,
  input  C,
  input  D,
  input  Sel0,
  input  Sel1,
  output S
);

  wire n2_mux_1_y, n2_mux_2_y;

  _2_MUX u_2_mux_1 (.A(A), .B(B), .Sel(Sel0), .Y(n2_mux_1_y));
  _2_MUX u_2_mux_2 (.A(C), .B(D), .Sel(Sel0), .Y(n2_mux_2_y));
  _2_MUX u_2_mux_3 (.A(n2_mux_1_y), .B(n2_mux_2_y), .Sel(Sel1), .Y(S));
endmodule

module _1_Bit_ALU (
  input  A,
  input  B,
  input  C,
  input  S0,
  input  S1,
  output S,
  output Cout
);

  wire and_1_out, and_2_out, fulladder_1_s, n2_mux_1_y, not_1_out, not_2_out, not_3_out, or_1_out;

  not not_1 (not_1_out, B);
  _2_MUX u_2_mux_1 (.A(not_1_out), .B(B), .Sel(and_1_out), .Y(n2_mux_1_y));
  and and_1 (and_1_out, not_2_out, not_3_out);
  or or_1 (or_1_out, A, B);
  and and_2 (and_2_out, A, B);
  FullAdder fulladder_1 (.A(A), .B(n2_mux_1_y), .C(C), .S(fulladder_1_s), .C_2(Cout));
  not not_2 (not_2_out, S0);
  not not_3 (not_3_out, S1);
  _4_MUX u_4_mux_1 (.A(fulladder_1_s), .B(and_2_out), .C(or_1_out), .D(fulladder_1_s), .Sel0(S0), .Sel1(S1), .S(S));
endmodule

module _4_bit_Ripple (
  input  Cin,
  input  [3:0] A0,
  input  [3:0] B0,
  input  S1,
  input  S0,
  output [3:0] S0_2,
  output Cout
);

  wire n1_bit_alu_1_cout, n1_bit_alu_2_cout, n1_bit_alu_3_cout;

  _1_Bit_ALU u_1_bit_alu_1 (.A(A0[0]), .B(B0[0]), .C(Cin), .S0(S0), .S1(S1), .S(S0_2[0]), .Cout(n1_bit_alu_1_cout));
  _1_Bit_ALU u_1_bit_alu_2 (
    .A(A0[1]), .B(B0[1]), .C(n1_bit_alu_1_cout), .S0(S0), .S1(S1), .S(S0_2[1]), .Cout(n1_bit_alu_2_cout));
  _1_Bit_ALU u_1_bit_alu_3 (
    .A(A0[2]), .B(B0[2]), .C(n1_bit_alu_2_cout), .S0(S0), .S1(S1), .S(S0_2[2]), .Cout(n1_bit_alu_3_cout));
  _1_Bit_ALU u_1_bit_alu_4 (.A(A0[3]), .B(B0[3]), .C(n1_bit_alu_3_cout), .S0(S0), .S1(S1), .S(S0_2[3]), .Cout(Cout));
endmodule

module Full_4_bit_ALU (
  input  [3:0] A0,
  input  [3:0] B0,
  input  S1,
  input  S0,
  output [3:0] S0_2,
  output Cout
);

  wire and_1_out, n1_bit_alu_1_cout, n1_bit_alu_2_cout, n1_bit_alu_3_cout;

  and and_1 (and_1_out, S0, S1);
  _1_Bit_ALU u_1_bit_alu_1 (
    .A(A0[0]), .B(B0[0]), .C(and_1_out), .S0(S0), .S1(S1), .S(S0_2[0]), .Cout(n1_bit_alu_1_cout));
  _1_Bit_ALU u_1_bit_alu_2 (
    .A(A0[1]), .B(B0[1]), .C(n1_bit_alu_1_cout), .S0(S0), .S1(S1), .S(S0_2[1]), .Cout(n1_bit_alu_2_cout));
  _1_Bit_ALU u_1_bit_alu_3 (
    .A(A0[2]), .B(B0[2]), .C(n1_bit_alu_2_cout), .S0(S0), .S1(S1), .S(S0_2[2]), .Cout(n1_bit_alu_3_cout));
  _1_Bit_ALU u_1_bit_alu_4 (.A(A0[3]), .B(B0[3]), .C(n1_bit_alu_3_cout), .S0(S0), .S1(S1), .S(S0_2[3]), .Cout(Cout));
endmodule
