// Logisim project Lab4.circ as structural Verilog
module _4_bit_ALU (
  input  [3:0] A,
  input  [3:0] B,
  input  [1:0] ALU_Op,
  output [3:0] ALU_Out
);

  wire and_1_out;
  wire [3:0] adder_1_out, and_2_out, multiplexer_1_out, not_1_out, or_1_out;

  Multiplexer #(.width(4), .enable("false")) multiplexer_1 (
    .in0(B), .in1(not_1_out), .out(multiplexer_1_out), .sel(and_1_out));
  assign not_1_out = ~B;  // NOT_Gate not_1, 4 bits wide
  and and_1 (and_1_out, ALU_Op[0], ALU_Op[1]);
  Adder #(.width(4)) adder_1 (.a(A), .b(multiplexer_1_out), .out(adder_1_out), .cin(and_1_out));  // open: cout
  assign and_2_out = multiplexer_1_out & A;  // AND_Gate and_2, 4 bits wide
  assign or_1_out = multiplexer_1_out | A;  // OR_Gate or_1, 4 bits wide
  Multiplexer #(.select(2), .width(4), .enable("false")) multiplexer_2 (
    .in0(adder_1_out), .in1(and_2_out), .in2(or_1_out), .in3(adder_1_out), .out(ALU_Out), .sel(ALU_Op));

  // Notes on the sheet:
  //   4 Bit ALU
  //   00 = ADD
  //   01 = AND
  //   10 = OR
  //   11 = SUB
  //   sub not B
  //   sub cin
  //   sub
endmodule

module _8x4_bit_Register_File (
  input  [3:0] Data_In,
  input  [2:0] Read_Addr_1,
  input  Write_Enable,
  input  [2:0] Write_Addr,
  input  [2:0] Read_Addr_2,
  input  Clock,
  output [3:0] Read_1_Data,
  output [3:0] Read_2_Data
);

  wire demultiplexer_1_out0, demultiplexer_1_out1, demultiplexer_1_out2, demultiplexer_1_out3,
       demultiplexer_1_out4, demultiplexer_1_out5, demultiplexer_1_out6, demultiplexer_1_out7;
  wire [3:0] register_1_q, register_2_q, register_3_q, register_4_q, register_5_q, register_6_q,
       register_7_q, register_8_q;

  Demultiplexer #(.select(3), .enable("false")) demultiplexer_1 (
    .out0(demultiplexer_1_out0), .out1(demultiplexer_1_out1), .out2(demultiplexer_1_out2),
    .out3(demultiplexer_1_out3), .out4(demultiplexer_1_out4), .out5(demultiplexer_1_out5),
    .out6(demultiplexer_1_out6), .out7(demultiplexer_1_out7), .in(Write_Enable), .sel(Write_Addr));
  Register #(.width(4)) register_1 (
    .D(Data_In), .en(demultiplexer_1_out0), .Q(register_1_q), .clk(Clock));  // open: clr
  Register #(.width(4)) register_2 (
    .D(Data_In), .en(demultiplexer_1_out1), .Q(register_2_q), .clk(Clock));  // open: clr
  Register #(.width(4)) register_3 (
    .D(Data_In), .en(demultiplexer_1_out2), .Q(register_3_q), .clk(Clock));  // open: clr
  Register #(.width(4)) register_4 (
    .D(Data_In), .en(demultiplexer_1_out3), .Q(register_4_q), .clk(Clock));  // open: clr
  Register #(.width(4)) register_5 (
    .D(Data_In), .en(demultiplexer_1_out4), .Q(register_5_q), .clk(Clock));  // open: clr
  Register #(.width(4)) register_6 (
    .D(Data_In), .en(demultiplexer_1_out5), .Q(register_6_q), .clk(Clock));  // open: clr
  Register #(.width(4)) register_7 (
    .D(Data_In), .en(demultiplexer_1_out6), .Q(register_7_q), .clk(Clock));  // open: clr
  Register #(.width(4)) register_8 (
    .D(Data_In), .en(demultiplexer_1_out7), .Q(register_8_q), .clk(Clock));  // open: clr
  Multiplexer #(.select(3), .width(4), .enable("false")) multiplexer_1 (
    .in0(register_1_q), .in1(register_2_q), .in2(register_3_q), .in3(register_4_q), .in4(register_5_q),
    .in5(register_6_q), .in6(register_7_q), .in7(register_8_q), .out(Read_1_Data), .sel(Read_Addr_1));
  Multiplexer #(.select(3), .width(4), .enable("false")) multiplexer_2 (
    .in0(register_1_q), .in1(register_2_q), .in2(register_3_q), .in3(register_4_q), .in4(register_5_q),
    .in5(register_6_q), .in6(register_7_q), .in7(register_8_q), .out(Read_2_Data), .sel(Read_Addr_2));

  // Notes on the sheet:
  //   8x4-bit Register File
endmodule

module ALU_REG_Instruction (
  input  [13:0] in_1,
  input  clock,
  output [3:0] CPU_Op_Out
);

  wire [3:0] bit_extender_1_out, multiplexer_1_out, n8x4_bit_register_file_1_read_1_data,
       n8x4_bit_register_file_1_read_2_data;

  _8x4_bit_Register_File u_8x4_bit_register_file_1 (
    .Data_In(CPU_Op_Out), .Write_Enable(1'b1), .Clock(clock), .Write_Addr(in_1[8:6]),
    .Read_Addr_1(in_1[5:3]), .Read_Addr_2(in_1[2:0]), .Read_1_Data(n8x4_bit_register_file_1_read_1_data),
    .Read_2_Data(n8x4_bit_register_file_1_read_2_data));
  Multiplexer #(.width(4), .enable("false")) multiplexer_1 (
    .in0(n8x4_bit_register_file_1_read_2_data), .in1(bit_extender_1_out), .out(multiplexer_1_out),
    .sel(in_1[13]));
  assign bit_extender_1_out = {{1{in_1[2]}}, in_1[2:0]};  // Bit_Extender bit_extender_1
  _4_bit_ALU u_4_bit_alu_1 (
    .A(n8x4_bit_register_file_1_read_1_data), .B(multiplexer_1_out), .ALU_Op(in_1[10:9]), .ALU_Out(CPU_Op_Out));

  // Notes on the sheet:
  //   op
  //   src2
  //   src1
  //   immed data
  //   immed select
  //   ALU op
  //   dest
endmodule

module ALU_With_Mem (
  input  [13:0] in_1,
  input  clock,
  output [3:0] CPU_Op_Out
);

  wire control_module_1_is, control_module_1_lw, control_module_1_sw, not_1_out;
  wire [1:0] control_module_1_alusl;
  wire [2:0] multiplexer_1_out;
  wire [3:0] bit_extender_1_out, multiplexer_2_out, multiplexer_3_out, n8x4_bit_register_file_1_read_1_data,
       n8x4_bit_register_file_1_read_2_data, ram_1_data;

  not not_1 (not_1_out, control_module_1_sw);
  Control_Module control_module_1 (
    .in_1(in_1[13:9]), .IS(control_module_1_is), .LW(control_module_1_lw), .SW(control_module_1_sw),
    .ALUsl(control_module_1_alusl));
  Multiplexer #(.width(3), .enable("false")) multiplexer_1 (
    .in0(in_1[2:0]), .in1(in_1[8:6]), .out(multiplexer_1_out), .sel(control_module_1_sw));
  _8x4_bit_Register_File u_8x4_bit_register_file_1 (
    .Data_In(multiplexer_3_out), .Write_Enable(not_1_out), .Clock(clock), .Write_Addr(in_1[8:6]),
    .Read_Addr_1(in_1[5:3]), .Read_Addr_2(multiplexer_1_out),
    .Read_1_Data(n8x4_bit_register_file_1_read_1_data), .Read_2_Data(n8x4_bit_register_file_1_read_2_data));
  Multiplexer #(.width(4), .enable("false")) multiplexer_2 (
    .in0(n8x4_bit_register_file_1_read_2_data), .in1(bit_extender_1_out), .out(multiplexer_2_out),
    .sel(control_module_1_is));
  assign bit_extender_1_out = {{1{in_1[2]}}, in_1[2:0]};  // Bit_Extender bit_extender_1
  _4_bit_ALU u_4_bit_alu_1 (
    .A(n8x4_bit_register_file_1_read_1_data), .B(multiplexer_2_out), .ALU_Op(control_module_1_alusl),
    .ALU_Out(CPU_Op_Out));
  Multiplexer #(.width(4), .enable("false")) multiplexer_3 (
    .in0(CPU_Op_Out), .in1(ram_1_data), .out(multiplexer_3_out), .sel(control_module_1_lw));
  RAM #(.addrWidth(4), .dataWidth(4), .bus("separate")) ram_1 (
    .addr(CPU_Op_Out), .din(n8x4_bit_register_file_1_read_2_data), .data(ram_1_data),
    .str(control_module_1_sw), .sel(1'b1), .clk(clock), .ld(control_module_1_lw));  // open: clr

  // Notes on the sheet:
  //   op
  //   src2
  //   src1
  //   immed data
  //   immed select
  //   ALU op
  //   dest
endmodule

module Control_Module (
  input  [4:0] in_1,
  output IS,
  output LW,
  output SW,
  output [1:0] ALUsl
);


  assign ALUsl = in_1[1:0];
  assign IS = in_1[4];
  assign LW = in_1[3];
  assign SW = in_1[2];
endmodule

module ALU_With_Mem2 (
  input  clock,
  output [3:0] CPU_Op_Out
);

  wire control_module_1_is, control_module_1_lw, control_module_1_sw, not_1_out;
  wire [1:0] control_module_1_alusl;
  wire [2:0] multiplexer_1_out;
  wire [3:0] adder_1_out, bit_extender_1_out, multiplexer_2_out, multiplexer_3_out,
       n8x4_bit_register_file_1_read_1_data, n8x4_bit_register_file_1_read_2_data, ram_2_data, register_1_q;
  wire [13:0] ram_1_data;

  Adder #(.width(4)) adder_1 (.a(register_1_q), .b(4'b0001), .out(adder_1_out));  // open: cin, cout
  Register #(.width(4)) register_1 (.D(adder_1_out), .en(1'b1), .Q(register_1_q), .clk(clock));  // open: clr
  RAM #(.addrWidth(4), .dataWidth(14), .bus("separate")) ram_1 (
    .addr(register_1_q), .data(ram_1_data), .sel(1'b1), .ld(1'b1));  // open: din, str, clk, clr
  not not_1 (not_1_out, control_module_1_sw);
  Control_Module control_module_1 (
    .in_1(ram_1_data[13:9]), .IS(control_module_1_is), .LW(control_module_1_lw), .SW(control_module_1_sw),
    .ALUsl(control_module_1_alusl));
  Multiplexer #(.width(3), .enable("false")) multiplexer_1 (
    .in0(ram_1_data[2:0]), .in1(ram_1_data[8:6]), .out(multiplexer_1_out), .sel(control_module_1_sw));
  _8x4_bit_Register_File u_8x4_bit_register_file_1 (
    .Data_In(multiplexer_3_out), .Write_Enable(not_1_out), .Clock(clock), .Write_Addr(ram_1_data[8:6]),
    .Read_Addr_1(ram_1_data[5:3]), .Read_Addr_2(multiplexer_1_out),
    .Read_1_Data(n8x4_bit_register_file_1_read_1_data), .Read_2_Data(n8x4_bit_register_file_1_read_2_data));
  assign bit_extender_1_out = {{1{ram_1_data[2]}}, ram_1_data[2:0]};  // Bit_Extender bit_extender_1
  Multiplexer #(.width(4), .enable("false")) multiplexer_2 (
    .in0(n8x4_bit_register_file_1_read_2_data), .in1(bit_extender_1_out), .out(multiplexer_2_out),
    .sel(control_module_1_is));
  Multiplexer #(.width(4), .enable("false")) multiplexer_3 (
    .in0(CPU_Op_Out), .in1(ram_2_data), .out(multiplexer_3_out), .sel(control_module_1_lw));
  _4_bit_ALU u_4_bit_alu_1 (
    .A(n8x4_bit_register_file_1_read_1_data), .B(multiplexer_2_out), .ALU_Op(control_module_1_alusl),
    .ALU_Out(CPU_Op_Out));
  RAM #(.addrWidth(4), .dataWidth(4), .bus("separate")) ram_2 (
    .addr(CPU_Op_Out), .din(n8x4_bit_register_file_1_read_2_data), .data(ram_2_data),
    .str(control_module_1_sw), .sel(1'b1), .clk(clock), .ld(control_module_1_lw));  // open: clr

  // Notes on the sheet:
  //   src2
  //   ALU op
  //   dest
  //   src1
  //   immed data
  //   immed select
endmodule
